# Fritzing sketch e-11blaster (saved by Fritzing 0.9.2b)
breadboards: 1

parts:
  Trigger = Pushbutton [part_number=S1 package=THT]
  Mode = Pushbutton [part_number=S2 package=THT]
  Reload = Pushbutton [part_number=S3 package=THT]
  Arduino = Arduino Nano (Rev3.0) [part_number=AD1]
  part = DC Power [voltage=7.4V part_number=V1]
  part_2 = Resistor [tolerance=±5% resistance=220 part_number=R1 package=THT]
  Power_Indicator = LED - 5mm [color="Red (633nm)" part_number=LED3 package="5 mm [THT]"]
  Grove_10_Segment_LED = female pin header, 4 pins [form="♀ (female)" part_number=LED1]
  Ada_Fruit_NeoPixel = female pin header, 3 pins [form="♀ (female)" part_number=LED2]
  part_3 = Resistor [tolerance=±5% resistance=470 part_number=R2 package=THT]
  WT5001M02-28P = IC, DIP package, 28 pins [part_number=W1]
  Left_Speaker = Piezo Speaker [part_number=SP1]
  Right_Speaker = Piezo Speaker [part_number=SP2]
  3W_Mini_Amplifier = female pin header, 11 pins [form="♀ (female)" part_number=A1]

nets:
  N1: Trigger.leg0, Mode.leg0, Reload.leg0, Arduino.GND, part.V-, Power_Indicator.cathode, Grove_10_Segment_LED.pin1, Ada_Fruit_NeoPixel.pin3, WT5001M02-28P.pin14, 3W_Mini_Amplifier.pin5, 3W_Mini_Amplifier.pin10
  N2: Trigger.leg1, Arduino.D2
  N3: Mode.leg1, Arduino.D3
  N4: Reload.leg1, Arduino.D4
  N5: Arduino.D1/TX, WT5001M02-28P.pin17
  N6: Arduino.D5, Grove_10_Segment_LED.pin4
  N7: Arduino.D6, Grove_10_Segment_LED.pin3
  N8: Arduino.D7, part_3.Pin_0
  N9: Arduino.D11/MOSI, part_2.Pin_0
  N10: Arduino.VIN, part.V+
  N11: Arduino.5V, Grove_10_Segment_LED.pin2, Ada_Fruit_NeoPixel.pin1, WT5001M02-28P.pin22, 3W_Mini_Amplifier.pin6
  N12: part_2.Pin_1, Power_Indicator.anode
  N13: Ada_Fruit_NeoPixel.pin2, part_3.Pin_1
  N14: WT5001M02-28P.pin9, 3W_Mini_Amplifier.pin11
  N15: WT5001M02-28P.pin10, 3W_Mini_Amplifier.pin9
  N16: Left_Speaker.pin1, 3W_Mini_Amplifier.pin4
  N17: Left_Speaker.pin2, 3W_Mini_Amplifier.pin3
  N18: Right_Speaker.pin1, 3W_Mini_Amplifier.pin2
  N19: Right_Speaker.pin2, 3W_Mini_Amplifier.pin1

notes:
  https://github.com/themaninthesuitcase/e-11blaster
  Copyright © 2015 Chris Pearson. Available under MIT License.
